// Logisim project final_booth.circ as structural Verilog: 11 circuits, main circuit Booth's multiplier
module Booth_s_multiplier (
  input  [21:0] _22input,
  input  [21:0] _22_input,
  input  Reset
);

  wire A_out, clock_1_out, controller_1_c0, controller_1_c1, controller_1_cl__a__q_1, controller_1_dec_cnt,
       controller_1_load__m__q__cnt, controller_1_load_a, controller_1_shr, or_1_out, Q__1_q0, Q_out, Q_q21;
  wire [4:0] counter_1_q;
  wire [21:0] A_q21, M_q21, n22bit_alu_1_result;

  Clock clock_1 (.out(clock_1_out));
  Controller controller_1 (
    .Clk(clock_1_out), .Q0(Q_q21), .Q_1(Q__1_q0), .Count(counter_1_q), .C0(controller_1_c0),
    .C1(controller_1_c1), .Shr(controller_1_shr), .Dec_Cnt(controller_1_dec_cnt),
    .Cl__A__Q_1(controller_1_cl__a__q_1), .Load_A(controller_1_load_a),
    .LOad__M__Q__Cnt(controller_1_load__m__q__cnt), .Reset(Reset));
  or or_1 (or_1_out, controller_1_load__m__q__cnt, controller_1_dec_cnt);
  Counter #(.width(5), .max('h1a)) counter_1 (
    .load(or_1_out), .D(5'b11010), .count(controller_1_dec_cnt), .Q(counter_1_q), .clk(clock_1_out));  // open: carry, clr
  Shift_Register #(.length(22)) A (
    .shift(controller_1_shr), .in(A_q21[21]), .clk(clock_1_out), .out(A_out), .load(controller_1_load_a),
    .clr(controller_1_cl__a__q_1), .d0(n22bit_alu_1_result[21]), .q0(A_q21[21]),
    .d1(n22bit_alu_1_result[20]), .q1(A_q21[20]), .d2(n22bit_alu_1_result[19]), .q2(A_q21[19]),
    .d3(n22bit_alu_1_result[18]), .q3(A_q21[18]), .d4(n22bit_alu_1_result[17]), .q4(A_q21[17]),
    .d5(n22bit_alu_1_result[16]), .q5(A_q21[16]), .d6(n22bit_alu_1_result[15]), .q6(A_q21[15]),
    .d7(n22bit_alu_1_result[14]), .q7(A_q21[14]), .d8(n22bit_alu_1_result[13]), .q8(A_q21[13]),
    .d9(n22bit_alu_1_result[12]), .q9(A_q21[12]), .d10(n22bit_alu_1_result[11]), .q10(A_q21[11]),
    .d11(n22bit_alu_1_result[10]), .q11(A_q21[10]), .d12(n22bit_alu_1_result[9]), .q12(A_q21[9]),
    .d13(n22bit_alu_1_result[8]), .q13(A_q21[8]), .d14(n22bit_alu_1_result[7]), .q14(A_q21[7]),
    .d15(n22bit_alu_1_result[6]), .q15(A_q21[6]), .d16(n22bit_alu_1_result[5]), .q16(A_q21[5]),
    .d17(n22bit_alu_1_result[4]), .q17(A_q21[4]), .d18(n22bit_alu_1_result[3]), .q18(A_q21[3]),
    .d19(n22bit_alu_1_result[2]), .q19(A_q21[2]), .d20(n22bit_alu_1_result[1]), .q20(A_q21[1]),
    .d21(n22bit_alu_1_result[0]), .q21(A_q21[0]));
  Shift_Register #(.length(22)) M (
    .shift(1'b0), .clk(clock_1_out), .load(controller_1_load__m__q__cnt), .d0(_22input[21]), .q0(M_q21[21]),
    .d1(_22input[20]), .q1(M_q21[20]), .d2(_22input[19]), .q2(M_q21[19]), .d3(_22input[18]), .q3(M_q21[18]),
    .d4(_22input[17]), .q4(M_q21[17]), .d5(_22input[16]), .q5(M_q21[16]), .d6(_22input[15]), .q6(M_q21[15]),
    .d7(_22input[14]), .q7(M_q21[14]), .d8(_22input[13]), .q8(M_q21[13]), .d9(_22input[12]), .q9(M_q21[12]),
    .d10(_22input[11]), .q10(M_q21[11]), .d11(_22input[10]), .q11(M_q21[10]), .d12(_22input[9]),
    .q12(M_q21[9]), .d13(_22input[8]), .q13(M_q21[8]), .d14(_22input[7]), .q14(M_q21[7]), .d15(_22input[6]),
    .q15(M_q21[6]), .d16(_22input[5]), .q16(M_q21[5]), .d17(_22input[4]), .q17(M_q21[4]), .d18(_22input[3]),
    .q18(M_q21[3]), .d19(_22input[2]), .q19(M_q21[2]), .d20(_22input[1]), .q20(M_q21[1]), .d21(_22input[0]),
    .q21(M_q21[0]));  // open: in, out, clr
  _22bit_ALU u_22bit_alu_1 (
    .A(A_q21), .B(M_q21), .Result(n22bit_alu_1_result), .Control0(controller_1_c0), .Control1(controller_1_c1));  // open: Zero, Negative, Overflow, Carry
  Shift_Register #(.length(22)) Q (
    .shift(controller_1_shr), .in(A_out), .clk(clock_1_out), .out(Q_out),
    .load(controller_1_load__m__q__cnt), .d0(_22_input[21]), .d1(_22_input[20]), .d2(_22_input[19]),
    .d3(_22_input[18]), .d4(_22_input[17]), .d5(_22_input[16]), .d6(_22_input[15]), .d7(_22_input[14]),
    .d8(_22_input[13]), .d9(_22_input[12]), .d10(_22_input[11]), .d11(_22_input[10]), .d12(_22_input[9]),
    .d13(_22_input[8]), .d14(_22_input[7]), .d15(_22_input[6]), .d16(_22_input[5]), .d17(_22_input[4]),
    .d18(_22_input[3]), .d19(_22_input[2]), .d20(_22_input[1]), .d21(_22_input[0]), .q21(Q_q21));  // open: clr, q0, q1, q2, q3, q4, q5, q6, q7, q8, q9, q10, q11, q12, q13, q14, q15, q16, q17, q18, q19, q20
  Shift_Register #(.length(1)) Q__1 (
    .shift(controller_1_shr), .in(Q_out), .clk(clock_1_out), .clr(controller_1_cl__a__q_1), .q0(Q__1_q0));  // open: out, load, d0
endmodule

module _22_bit_OR (
  input  [21:0] A,
  input  [21:0] B,
  output [21:0] Result
);

  or or_1 (Result[0], A[0], B[0]);
  or or_2 (Result[1], A[1], B[1]);
  or or_3 (Result[2], A[2], B[2]);
  or or_4 (Result[3], A[3], B[3]);
  or or_5 (Result[4], A[4], B[4]);
  or or_6 (Result[5], A[5], B[5]);
  or or_7 (Result[6], A[6], B[6]);
  or or_8 (Result[7], A[7], B[7]);
  or or_9 (Result[8], A[8], B[8]);
  or or_10 (Result[9], A[9], B[9]);
  or or_11 (Result[10], A[10], B[10]);
  or or_12 (Result[11], A[11], B[11]);
  or or_13 (Result[12], A[12], B[12]);
  or or_14 (Result[13], A[13], B[13]);
  or or_15 (Result[14], A[14], B[14]);
  or or_16 (Result[15], A[15], B[15]);
  or or_17 (Result[16], A[16], B[16]);
  or or_18 (Result[17], A[17], B[17]);
  or or_19 (Result[18], A[18], B[18]);
  or or_20 (Result[19], A[19], B[19]);
  or or_21 (Result[20], A[20], B[20]);
  or or_22 (Result[21], A[21], B[21]);
endmodule

module _22_bit_AND (
  input  [21:0] A,
  input  [21:0] B,
  output [21:0] Result
);

  and and_1 (Result[0], A[0], B[0]);
  and and_2 (Result[1], A[1], B[1]);
  and and_3 (Result[2], A[2], B[2]);
  and and_4 (Result[3], A[3], B[3]);
  and and_5 (Result[4], A[4], B[4]);
  and and_6 (Result[5], A[5], B[5]);
  and and_7 (Result[6], A[6], B[6]);
  and and_8 (Result[7], A[7], B[7]);
  and and_9 (Result[8], A[8], B[8]);
  and and_10 (Result[9], A[9], B[9]);
  and and_11 (Result[10], A[10], B[10]);
  and and_12 (Result[11], A[11], B[11]);
  and and_13 (Result[12], A[12], B[12]);
  and and_14 (Result[13], A[13], B[13]);
  and and_15 (Result[14], A[14], B[14]);
  and and_16 (Result[15], A[15], B[15]);
  and and_17 (Result[16], A[16], B[16]);
  and and_18 (Result[17], A[17], B[17]);
  and and_19 (Result[18], A[18], B[18]);
  and and_20 (Result[19], A[19], B[19]);
  and and_21 (Result[20], A[20], B[20]);
  and and_22 (Result[21], A[21], B[21]);
endmodule

module Full_adder (
  input  Carry_in,
  input  A,
  input  B,
  output Result,
  output Carry_out
);

  wire and_1_out, and_2_out, xor_1_out;

  and and_1 (and_1_out, B, A);
  xor xor_1 (xor_1_out, A, B);
  or or_1 (Carry_out, and_1_out, and_2_out);
  and and_2 (and_2_out, xor_1_out, Carry_in);
  xor xor_2 (Result, Carry_in, xor_1_out);
endmodule

module _22_bit_full_adder (
  input  Carry_in,
  input  [21:0] A,
  input  [21:0] B,
  output [21:0] Result,
  output Carry
);

  wire full_adder_1_carry_out, full_adder_2_carry_out, full_adder_3_carry_out, full_adder_4_carry_out,
       full_adder_5_carry_out, full_adder_6_carry_out, full_adder_7_carry_out, full_adder_8_carry_out,
       full_adder_9_carry_out, full_adder_10_carry_out, full_adder_11_carry_out, full_adder_12_carry_out,
       full_adder_13_carry_out, full_adder_14_carry_out, full_adder_15_carry_out, full_adder_16_carry_out,
       full_adder_17_carry_out, full_adder_18_carry_out, full_adder_19_carry_out, full_adder_20_carry_out,
       full_adder_21_carry_out;

  Full_adder full_adder_1 (
    .Carry_in(Carry_in), .A(A[0]), .B(B[0]), .Result(Result[0]), .Carry_out(full_adder_1_carry_out));
  Full_adder full_adder_2 (
    .Carry_in(full_adder_1_carry_out), .A(A[1]), .B(B[1]), .Result(Result[1]),
    .Carry_out(full_adder_2_carry_out));
  Full_adder full_adder_3 (
    .Carry_in(full_adder_2_carry_out), .A(A[2]), .B(B[2]), .Result(Result[2]),
    .Carry_out(full_adder_3_carry_out));
  Full_adder full_adder_4 (
    .Carry_in(full_adder_3_carry_out), .A(A[3]), .B(B[3]), .Result(Result[3]),
    .Carry_out(full_adder_4_carry_out));
  Full_adder full_adder_5 (
    .Carry_in(full_adder_4_carry_out), .A(A[4]), .B(B[4]), .Result(Result[4]),
    .Carry_out(full_adder_5_carry_out));
  Full_adder full_adder_6 (
    .Carry_in(full_adder_5_carry_out), .A(A[5]), .B(B[5]), .Result(Result[5]),
    .Carry_out(full_adder_6_carry_out));
  Full_adder full_adder_7 (
    .Carry_in(full_adder_6_carry_out), .A(A[6]), .B(B[6]), .Result(Result[6]),
    .Carry_out(full_adder_7_carry_out));
  Full_adder full_adder_8 (
    .Carry_in(full_adder_7_carry_out), .A(A[7]), .B(B[7]), .Result(Result[7]),
    .Carry_out(full_adder_8_carry_out));
  Full_adder full_adder_9 (
    .Carry_in(full_adder_8_carry_out), .A(A[8]), .B(B[8]), .Result(Result[8]),
    .Carry_out(full_adder_9_carry_out));
  Full_adder full_adder_10 (
    .Carry_in(full_adder_9_carry_out), .A(A[9]), .B(B[9]), .Result(Result[9]),
    .Carry_out(full_adder_10_carry_out));
  Full_adder full_adder_11 (
    .Carry_in(full_adder_10_carry_out), .A(A[10]), .B(B[10]), .Result(Result[10]),
    .Carry_out(full_adder_11_carry_out));
  Full_adder full_adder_12 (
    .Carry_in(full_adder_11_carry_out), .A(A[11]), .B(B[11]), .Result(Result[11]),
    .Carry_out(full_adder_12_carry_out));
  Full_adder full_adder_13 (
    .Carry_in(full_adder_12_carry_out), .A(A[12]), .B(B[12]), .Result(Result[12]),
    .Carry_out(full_adder_13_carry_out));
  Full_adder full_adder_14 (
    .Carry_in(full_adder_13_carry_out), .A(A[13]), .B(B[13]), .Result(Result[13]),
    .Carry_out(full_adder_14_carry_out));
  Full_adder full_adder_15 (
    .Carry_in(full_adder_14_carry_out), .A(A[14]), .B(B[14]), .Result(Result[14]),
    .Carry_out(full_adder_15_carry_out));
  Full_adder full_adder_16 (
    .Carry_in(full_adder_15_carry_out), .A(A[15]), .B(B[15]), .Result(Result[15]),
    .Carry_out(full_adder_16_carry_out));
  Full_adder full_adder_17 (
    .Carry_in(full_adder_16_carry_out), .A(A[16]), .B(B[16]), .Result(Result[16]),
    .Carry_out(full_adder_17_carry_out));
  Full_adder full_adder_18 (
    .Carry_in(full_adder_17_carry_out), .A(A[17]), .B(B[17]), .Result(Result[17]),
    .Carry_out(full_adder_18_carry_out));
  Full_adder full_adder_19 (
    .Carry_in(full_adder_18_carry_out), .A(A[18]), .B(B[18]), .Result(Result[18]),
    .Carry_out(full_adder_19_carry_out));
  Full_adder full_adder_20 (
    .Carry_in(full_adder_19_carry_out), .A(A[19]), .B(B[19]), .Result(Result[19]),
    .Carry_out(full_adder_20_carry_out));
  Full_adder full_adder_21 (
    .Carry_in(full_adder_20_carry_out), .A(A[20]), .B(B[20]), .Result(Result[20]),
    .Carry_out(full_adder_21_carry_out));
  Full_adder full_adder_22 (
    .Carry_in(full_adder_21_carry_out), .A(A[21]), .B(B[21]), .Result(Result[21]), .Carry_out(Carry));
endmodule

module _22_bit_xor (
  input  Control,
  input  [21:0] B,
  output [21:0] Result
);

  wire [21:0] bit_extender_1_out;

  assign bit_extender_1_out = {{21{Control}}, Control};  // Bit_Extender bit_extender_1
  xor xor_1 (Result[0], bit_extender_1_out[0], B[0]);
  xor xor_2 (Result[1], bit_extender_1_out[1], B[1]);
  xor xor_3 (Result[2], bit_extender_1_out[2], B[2]);
  xor xor_4 (Result[3], bit_extender_1_out[3], B[3]);
  xor xor_5 (Result[4], bit_extender_1_out[4], B[4]);
  xor xor_6 (Result[5], bit_extender_1_out[5], B[5]);
  xor xor_7 (Result[6], bit_extender_1_out[6], B[6]);
  xor xor_8 (Result[7], bit_extender_1_out[7], B[7]);
  xor xor_9 (Result[8], bit_extender_1_out[8], B[8]);
  xor xor_10 (Result[9], bit_extender_1_out[9], B[9]);
  xor xor_11 (Result[10], bit_extender_1_out[10], B[10]);
  xor xor_12 (Result[11], bit_extender_1_out[11], B[11]);
  xor xor_13 (Result[12], bit_extender_1_out[12], B[12]);
  xor xor_14 (Result[13], bit_extender_1_out[13], B[13]);
  xor xor_15 (Result[14], bit_extender_1_out[14], B[14]);
  xor xor_16 (Result[15], bit_extender_1_out[15], B[15]);
  xor xor_17 (Result[16], bit_extender_1_out[16], B[16]);
  xor xor_18 (Result[17], bit_extender_1_out[17], B[17]);
  xor xor_19 (Result[18], bit_extender_1_out[18], B[18]);
  xor xor_20 (Result[19], bit_extender_1_out[19], B[19]);
  xor xor_21 (Result[20], bit_extender_1_out[20], B[20]);
  xor xor_22 (Result[21], bit_extender_1_out[21], B[21]);
endmodule

// 22-bit \nADD/SUB
module _22_bit_Add_sub (
  input  Sub,
  input  [21:0] A,
  input  [21:0] B,
  output [21:0] Result,
  output Carry,
  output Overflow
);

  wire and_1_out, and_2_out, not_1_out, not_2_out, not_3_out, sign_bit_out_1_ms_bit, sign_bit_out_2_ms_bit,
       sign_bit_out_3_ms_bit;
  wire [21:0] n22_bit_xor_1_result;

  sign_bit_out sign_bit_out_1 (.Input(A), .MS_bit(sign_bit_out_1_ms_bit));
  not not_1 (not_1_out, sign_bit_out_1_ms_bit);
  _22_bit_xor u_22_bit_xor_1 (.Control(Sub), .Result(n22_bit_xor_1_result), .B(B));
  sign_bit_out sign_bit_out_2 (.Input(n22_bit_xor_1_result), .MS_bit(sign_bit_out_2_ms_bit));
  not not_2 (not_2_out, sign_bit_out_2_ms_bit);
  _22_bit_full_adder u_22_bit_full_adder_1 (
    .A(A), .B(n22_bit_xor_1_result), .Result(Result), .Carry_in(Sub), .Carry(Carry));
  sign_bit_out sign_bit_out_3 (.Input(Result), .MS_bit(sign_bit_out_3_ms_bit));
  not not_3 (not_3_out, sign_bit_out_3_ms_bit);
  and and_1 (and_1_out, not_3_out, sign_bit_out_2_ms_bit, sign_bit_out_1_ms_bit);
  and and_2 (and_2_out, sign_bit_out_3_ms_bit, not_2_out, not_1_out);
  or or_1 (Overflow, and_1_out, and_2_out);

  // Notes on the sheet:
  //   A25
  //   B25
  //   Result 21
endmodule

// 21th
module sign_bit_out (
  input  [21:0] Input,
  output MS_bit
);


  assign MS_bit = Input[21];
endmodule

// Reduce-OR
module _22_bit_reduce_or (
  input  [21:0] Input,
  output Output
);

  or or_1 (Output, Input[0], Input[1], Input[2], Input[3], Input[4], Input[5], Input[6], Input[7], Input[8], Input[9], Input[10], Input[11], Input[12], Input[13], Input[14], Input[15], Input[16], Input[17], Input[18], Input[19], Input[20], Input[21]);
endmodule

module _22bit_ALU (
  input  Control0,
  input  Control1,
  input  [21:0] A,
  input  [21:0] B,
  output [21:0] Result,
  output Zero,
  output Negative,
  output Overflow,
  output Carry
);

  wire n22_bit_reduce_or_1_output;
  wire [21:0] multiplexer_1_out, n22_bit_add_sub_1_result, n22_bit_and_1_result, n22_bit_or_1_result;

  _22_bit_AND u_22_bit_and_1 (.A(A), .B(B), .Result(n22_bit_and_1_result));
  _22_bit_OR u_22_bit_or_1 (.A(A), .Result(n22_bit_or_1_result), .B(B));
  _22_bit_Add_sub u_22_bit_add_sub_1 (
    .Sub(Control0), .A(A), .B(B), .Result(n22_bit_add_sub_1_result), .Carry(Carry), .Overflow(Overflow));
  Multiplexer #(.width(22), .enable("false")) multiplexer_1 (
    .in0(n22_bit_and_1_result), .in1(n22_bit_or_1_result), .out(multiplexer_1_out), .sel(Control0));
  Multiplexer #(.width(22), .enable("false")) multiplexer_2 (
    .in0(multiplexer_1_out), .in1(n22_bit_add_sub_1_result), .out(Result), .sel(Control1));
  sign_bit_out sign_bit_out_1 (.Input(Result), .MS_bit(Negative));
  _22_bit_reduce_or u_22_bit_reduce_or_1 (.Input(Result), .Output(n22_bit_reduce_or_1_output));
  not not_1 (Zero, n22_bit_reduce_or_1_output);

  // Notes on the sheet:
  //   10 :: OR
  //   00 ::AND
  //   01 :: ADD
  //   11 :: SUB
endmodule

// Control \nUnit
module Controller (
  input  Clk,
  input  Reset,
  input  Q0,
  input  Q_1,
  input  [4:0] Count,
  output Cl__A__Q_1,
  output LOad__M__Q__Cnt,
  output Load_A,
  output C0,
  output C1,
  output Shr,
  output Dec_Cnt
);

  wire and_3_out, multiplexer_1_out, not_1_out, not_2_out, not_3_out, not_4_out, not_5_out, not_6_out,
       not_7_out, or_2_out, Q0_prime_Q_1_out, Q0Q_1_prime_out;
  wire [1:0] rom_1_data_2;
  wire [2:0] and_1_out, and_2_out, bit_extender_1_out, bit_extender_2_out, bit_extender_3_out, CAR_q,
       or_1_out, rom_1_data;

  assign bit_extender_1_out = {{2{Q0_prime_Q_1_out}}, Q0_prime_Q_1_out};  // Bit_Extender bit_extender_1
  and Q0_prime_Q_1 (Q0_prime_Q_1_out, not_2_out, Q_1);
  not not_1 (not_1_out, Q0_prime_Q_1_out);
  assign bit_extender_2_out = {{2{not_1_out}}, not_1_out};  // Bit_Extender bit_extender_2
  assign and_1_out = 3'b100 & bit_extender_3_out & bit_extender_1_out;  // AND_Gate and_1, 3 bits wide
  assign or_1_out = and_1_out | rom_1_data | and_2_out;  // OR_Gate or_1, 3 bits wide
  not not_2 (not_2_out, Q0);
  assign and_2_out = bit_extender_2_out & bit_extender_3_out & 3'b101;  // AND_Gate and_2, 3 bits wide
  assign bit_extender_3_out = {{2{and_3_out}}, and_3_out};  // Bit_Extender bit_extender_3
  and and_3 (and_3_out, not_3_out, CAR_q[1], not_4_out);
  not not_3 (not_3_out, CAR_q[2]);
  not not_4 (not_4_out, CAR_q[0]);
  Counter #(.width(3), .max('h7)) CAR (
    .load(not_5_out), .D(or_1_out), .count(multiplexer_1_out), .Q(CAR_q), .clk(Clk), .clr(Reset));  // open: carry
  not not_5 (not_5_out, multiplexer_1_out);
  Multiplexer #(.select(2), .enable("false")) multiplexer_1 (
    .in0(1'b0), .in1(1'b1), .in2(Q0Q_1_prime_out), .in3(not_7_out), .out(multiplexer_1_out),
    .sel(rom_1_data_2));
  ROM #(.addrWidth(3), .dataWidth(12)) rom_1 (
    .addr(CAR_q), .data({Cl__A__Q_1, LOad__M__Q__Cnt, Load_A, C0, C1, Shr, Dec_Cnt, rom_1_data, rom_1_data_2}));  // open: sel
  and Q0Q_1_prime (Q0Q_1_prime_out, not_6_out, Q0);
  not not_6 (not_6_out, Q_1);
  or or_2 (or_2_out, Count[0], Count[1], Count[2], Count[3], Count[4]);
  not not_7 (not_7_out, or_2_out);

  // Notes on the sheet:
  //   To choose only
  //   state 2 (010)
  //   Control Word Format: Clear (A, Q-1), Load (M, Q, Cnt), Load A, C0, C1, Shr, Dec Cnt, Address bits (3 bit), Selection bits (2 bit)
  //   contents of rom_1 (hex, n*v repeats v):
  //   1 c01 2 394 281 61 b 1c
endmodule
