// Logisim project load-control--[D-E-B-E-D].circ as structural Verilog: 1 circuit, main circuit main
module main (
  input  in_1,
  input  in_2,
  output [21:0] OUTPUT,
  output [21:0] OUTPUT_2,
  output [21:0] OUTPUT_3,
  output [21:0] OUTPUT_4,
  output [21:0] OUTPUT_5
);

  wire clock_1_out;
  wire [1:0] counter_1_q;
  wire [5:0] rom_1_data;
  wire [21:0] controlled_buffer_1_out, controlled_buffer_2_out, controlled_buffer_3_out,
       controlled_buffer_4_out, controlled_buffer_5_out, controlled_buffer_6_out, controlled_buffer_7_out,
       controlled_buffer_8_out, undriven, undriven_2;

  Clock clock_1 (.out(clock_1_out));
  Counter #(.width(2), .max('h3)) counter_1 (
    .Q(counter_1_q), .clk(clock_1_out), .clr(in_1));  // open: load, D, count, carry
  ROM #(.addrWidth(2), .dataWidth(6)) rom_1 (.addr(counter_1_q), .data(rom_1_data));  // open: sel
  assign controlled_buffer_1_out = 1'b0 ? undriven : 22'bz;  // Controlled_Buffer controlled_buffer_1
  assign controlled_buffer_2_out = rom_1_data[2] ? controlled_buffer_7_out : 22'bz;  // Controlled_Buffer controlled_buffer_2
  assign controlled_buffer_3_out = 1'b0 ? undriven_2 : 22'bz;  // Controlled_Buffer controlled_buffer_3
  assign controlled_buffer_4_out = rom_1_data[1] ? controlled_buffer_7_out : 22'bz;  // Controlled_Buffer controlled_buffer_4
  assign controlled_buffer_5_out = rom_1_data[0] ? controlled_buffer_7_out : 22'bz;  // Controlled_Buffer controlled_buffer_5
  Register #(.width(22)) A (.D(controlled_buffer_1_out), .en(1'b1), .Q(OUTPUT), .clk(clock_1_out), .clr(in_2));
  Register #(.width(22)) B (.D(controlled_buffer_2_out), .en(1'b1), .Q(OUTPUT_2), .clk(clock_1_out), .clr(in_2));
  Register #(.width(22)) C (.D(controlled_buffer_3_out), .en(1'b1), .Q(OUTPUT_3), .clk(clock_1_out), .clr(in_2));
  Register #(.width(22)) D (.D(controlled_buffer_4_out), .en(1'b1), .Q(OUTPUT_4), .clk(clock_1_out), .clr(in_2));
  Register #(.width(22)) E (.D(controlled_buffer_5_out), .en(1'b1), .Q(OUTPUT_5), .clk(clock_1_out), .clr(in_2));
  assign controlled_buffer_6_out = 1'b0 ? OUTPUT : 22'bz;  // Controlled_Buffer controlled_buffer_6
  assign controlled_buffer_7_out = rom_1_data[5] ? OUTPUT_2 : 22'bz;  // Controlled_Buffer controlled_buffer_7
  assign controlled_buffer_8_out = 1'b0 ? OUTPUT_3 : 22'bz;  // Controlled_Buffer controlled_buffer_8
  assign controlled_buffer_7_out = rom_1_data[4] ? OUTPUT_4 : 22'bz;  // Controlled_Buffer controlled_buffer_9
  assign controlled_buffer_7_out = rom_1_data[3] ? OUTPUT_5 : 22'bz;  // Controlled_Buffer controlled_buffer_10

  // Notes on the sheet:
  //   contents of rom_1 (hex, n*v repeats v):
  //   11 c 21 a
endmodule
